// Logisim project all.circ as structural Verilog
module main (
  input  x,
  input  y,
  input  Cin,
  output Sum,
  output Cout
);

  wire and_1_out, and_3_out, and_4_out, not_1_out, not_2_out, not_3_out, not_4_out, not_5_out, not_6_out,
       or_1_out, or_2_out, or_3_out, or_4_out, or_5_out, or_6_out, or_7_out, or_8_out, or_9_out, or_10_out,
       or_11_out;

  not not_1 (not_1_out, y);
  not not_2 (not_2_out, x);
  not not_3 (not_3_out, x);
  not not_4 (not_4_out, y);
  or or_1 (or_1_out, x, y);
  or or_2 (or_2_out, x, Cin);
  or or_3 (or_3_out, x, y);
  or or_4 (or_4_out, x, not_1_out);
  not not_5 (not_5_out, Cin);
  or or_5 (or_5_out, not_2_out, y);
  not not_6 (not_6_out, Cin);
  or or_6 (or_6_out, not_3_out, not_4_out);
  and and_1 (and_1_out, or_1_out, or_2_out);
  or or_7 (or_7_out, y, Cin);
  or or_8 (or_8_out, or_3_out, Cin);
  or or_9 (or_9_out, or_4_out, not_5_out);
  or or_10 (or_10_out, or_5_out, not_6_out);
  or or_11 (or_11_out, or_6_out, Cin);
  and and_2 (Cout, and_1_out, or_7_out);
  and and_3 (and_3_out, or_8_out, or_9_out);
  and and_4 (and_4_out, or_10_out, or_11_out);
  and and_5 (Sum, and_3_out, and_4_out);
endmodule

module test (
  input  x,
  input  y,
  output z
);

  wire and_1_out, or_1_out;

  and and_1 (and_1_out, x, y);
  or or_1 (or_1_out, x, y);
  and and_2 (z, and_1_out, or_1_out);
endmodule

module toy (
  input  x,
  input  y,
  output z
);

  and and_1 (z, x, y);
endmodule
