// Logisim project single_cycle_mips_cpu.circ as structural Verilog
module IFU (
  input  CLK,
  input  Reset,
  output [31:0] Instr
);

  wire [29:0] adder_1_out, register_1_q;

  Clock clock_1 ();  // open: out
  Register #(.width(30)) register_1 (.D(adder_1_out), .Q(register_1_q), .clk(CLK), .clr(Reset));  // open: en
  // Probe on {register_1_q[2:0], 2'b00}
  Adder #(.width(30)) adder_1 (.a(register_1_q), .b(30'h1), .out(adder_1_out));  // open: cin, cout
  ROM #(.addrWidth(5), .dataWidth(32)) rom_1 (.addr({register_1_q[2:0], 2'b00}), .data(Instr));  // open: sel
  // Probe on Instr

  // Notes on the sheet:
  //   contents of rom_1 (hex, n*v repeats v):
  //   34125125 125213 12344 2151211 9034097 214412 123213 12521521 21321312 15425215 55521 222133
endmodule

module ALU (
  input  [31:0] operand1,
  input  [31:0] operand2,
  input  [2:0] ALUCtl,
  output [31:0] ALUOut,
  output Equal
);

  wire [31:0] adder_1_out, or_1_out, subtractor_1_out;

  Adder #(.width(32)) adder_1 (.a(operand1), .b(operand2), .out(adder_1_out));  // open: cin, cout
  Subtractor #(.width(32)) subtractor_1 (.a(operand1), .b(operand2), .out(subtractor_1_out));  // open: bin, bout
  assign or_1_out = operand1 | operand2;  // OR_Gate or_1, 32 bits wide
  Comparator #(.width(32), .mode("unsigned")) comparator_1 (.a(operand1), .b(operand2), .eq(Equal));  // open: gt, lt
  Multiplexer #(.select(3), .width(32)) multiplexer_1 (
    .in1(or_1_out), .in2(subtractor_1_out), .in4(adder_1_out), .out(ALUOut), .sel(ALUCtl));  // open: in0, in3, in5, in6, in7, en
  // Probe on operand1
  // Probe on operand2
  // Probe on ALUOut

  // Other names for the same wires on the sheet: op1[31:0] = operand1; op2[31:0] = operand2

  // Notes on the sheet:
  //   100  Add->4
  //   010  Sub->2
  //   001  OR->1
endmodule

module GRF (
  input  [4:0] RD1_num,
  input  [4:0] RD2_num,
  input  [4:0] W_num,
  input  [31:0] WD,
  input  in_5,
  input  in_6,
  input  WE,
  output [31:0] RD1,
  output [31:0] RD2
);

  wire WE1, WE2, WE3, WE4, WE5, WE6, WE7, WE8, WE9, WE10, WE11, WE12, WE13, WE14, WE15, WE16, WE17, WE18,
       WE19, WE20, WE21, WE22, WE23, WE24, WE25, WE26, WE27, WE28, WE29, WE30, WE31;
  wire [31:0] D1, D2, D3, D4, D5, D6, D7, D8, D9, D10, D11, D12, D13, D14, D15, D16, D17, D18, D19, D20, D21,
       D22, D23, D24, D25, D26, D27, D28, D29, D30, D31;

  Register #(.width(32)) R1 (.D(WD), .en(WE1), .Q(D1), .clk(in_5), .clr(in_6));
  Register #(.width(32)) R2 (.D(WD), .en(WE2), .Q(D2), .clk(in_5), .clr(in_6));
  Register #(.width(32)) R3 (.D(WD), .en(WE3), .Q(D3), .clk(in_5), .clr(in_6));
  Register #(.width(32)) R4 (.D(WD), .en(WE4), .Q(D4), .clk(in_5), .clr(in_6));
  Register #(.width(32)) R5 (.D(WD), .en(WE5), .Q(D5), .clk(in_5), .clr(in_6));
  Register #(.width(32)) R6 (.D(WD), .en(WE6), .Q(D6), .clk(in_5), .clr(in_6));
  Register #(.width(32)) R7 (.D(WD), .en(WE7), .Q(D7), .clk(in_5), .clr(in_6));
  // Probe on RD1
  Register #(.width(32)) R8 (.D(WD), .en(WE8), .Q(D8), .clk(in_5), .clr(in_6));
  Register #(.width(32)) R9 (.D(WD), .en(WE9), .Q(D9), .clk(in_5), .clr(in_6));
  Register #(.width(32)) R10 (.D(WD), .en(WE10), .Q(D10), .clk(in_5), .clr(in_6));
  Register #(.width(32)) R11 (.D(WD), .en(WE11), .Q(D11), .clk(in_5), .clr(in_6));
  Register #(.width(32)) R12 (.D(WD), .en(WE12), .Q(D12), .clk(in_5), .clr(in_6));
  Register #(.width(32)) R13 (.D(WD), .en(WE13), .Q(D13), .clk(in_5), .clr(in_6));
  Register #(.width(32)) R14 (.D(WD), .en(WE14), .Q(D14), .clk(in_5), .clr(in_6));
  Register #(.width(32)) R15 (.D(WD), .en(WE15), .Q(D15), .clk(in_5), .clr(in_6));
  // Probe on RD2
  Register #(.width(32)) R16 (.D(WD), .en(WE16), .Q(D16), .clk(in_5), .clr(in_6));
  Register #(.width(32)) R17 (.D(WD), .en(WE17), .Q(D17), .clk(in_5), .clr(in_6));
  Register #(.width(32)) R18 (.D(WD), .en(WE18), .Q(D18), .clk(in_5), .clr(in_6));
  Register #(.width(32)) R19 (.D(WD), .en(WE19), .Q(D19), .clk(in_5), .clr(in_6));
  Register #(.width(32)) R20 (.D(WD), .en(WE20), .Q(D20), .clk(in_5), .clr(in_6));
  Register #(.width(32)) R21 (.D(WD), .en(WE21), .Q(D21), .clk(in_5), .clr(in_6));
  Register #(.width(32)) R22 (.D(WD), .en(WE22), .Q(D22), .clk(in_5), .clr(in_6));
  Register #(.width(32)) R23 (.D(WD), .en(WE23), .Q(D23), .clk(in_5), .clr(in_6));
  Register #(.width(32)) R24 (.D(WD), .en(WE24), .Q(D24), .clk(in_5), .clr(in_6));
  Register #(.width(32)) R25 (.D(WD), .en(WE25), .Q(D25), .clk(in_5), .clr(in_6));
  Register #(.width(32)) R26 (.D(WD), .en(WE26), .Q(D26), .clk(in_5), .clr(in_6));
  Register #(.width(32)) R27 (.D(WD), .en(WE27), .Q(D27), .clk(in_5), .clr(in_6));
  Register #(.width(32)) R28 (.D(WD), .en(WE28), .Q(D28), .clk(in_5), .clr(in_6));
  Register #(.width(32)) R29 (.D(WD), .en(WE29), .Q(D29), .clk(in_5), .clr(in_6));
  Register #(.width(32)) R30 (.D(WD), .en(WE30), .Q(D30), .clk(in_5), .clr(in_6));
  Register #(.width(32)) R31 (.D(WD), .en(WE31), .Q(D31), .clk(in_5), .clr(in_6));
  Decoder #(.select(5), .disabled(0)) decoder_1 (
    .out1(WE1), .out2(WE2), .out3(WE3), .out4(WE4), .out5(WE5), .out6(WE6), .out7(WE7), .out8(WE8),
    .out9(WE9), .out10(WE10), .out11(WE11), .out12(WE12), .out13(WE13), .out14(WE14), .out15(WE15),
    .out16(WE16), .out17(WE17), .out18(WE18), .out19(WE19), .out20(WE20), .out21(WE21), .out22(WE22),
    .out23(WE23), .out24(WE24), .out25(WE25), .out26(WE26), .out27(WE27), .out28(WE28), .out29(WE29),
    .out30(WE30), .out31(WE31), .sel(W_num), .en(WE));  // open: out0
  Multiplexer #(.select(5), .width(32), .enable("false")) multiplexer_1 (
    .in0({32{1'b0}}), .in1(D1), .in2(D2), .in3(D3), .in4(D4), .in5(D5), .in6(D6), .in7(D7), .in8(D8),
    .in9(D9), .in10(D10), .in11(D11), .in12(D12), .in13(D13), .in14(D14), .in15(D15), .in16(D16), .in17(D17),
    .in18(D18), .in19(D19), .in20(D20), .in21(D21), .in22(D22), .in23(D23), .in24(D24), .in25(D25),
    .in26(D26), .in27(D27), .in28(D28), .in29(D29), .in30(D30), .in31(D31), .out(RD1), .sel(RD1_num));
  Multiplexer #(.select(5), .width(32), .enable("false")) multiplexer_2 (
    .in0({32{1'b0}}), .in1(D1), .in2(D2), .in3(D3), .in4(D4), .in5(D5), .in6(D6), .in7(D7), .in8(D8),
    .in9(D9), .in10(D10), .in11(D11), .in12(D12), .in13(D13), .in14(D14), .in15(D15), .in16(D16), .in17(D17),
    .in18(D18), .in19(D19), .in20(D20), .in21(D21), .in22(D22), .in23(D23), .in24(D24), .in25(D25),
    .in26(D26), .in27(D27), .in28(D28), .in29(D29), .in30(D30), .in31(D31), .out(RD2), .sel(RD2_num));

  // Other names for the same wires on the sheet: CLK = in_5; Out1[31:0] = RD1; Out2[31:0] = RD2; Reset = in_6;
  //   sel1[4:0] = RD1_num; sel2[4:0] = RD2_num; wsel[4:0] = W_num
endmodule

module DM (
  input  [31:0] MemAddr,
  input  [31:0] MemData,
  input  MemWrite,
  input  CLK,
  input  Reset,
  output [31:0] RdData
);

  wire buffer_1_out, not_1_out;

  buf buffer_1 (buffer_1_out, MemWrite);
  Clock clock_1 ();  // open: out
  not not_1 (not_1_out, MemWrite);
  RAM #(.addrWidth(5), .dataWidth(32), .bus("separate")) ram_1 (
    .addr(MemAddr[4:0]), .din(MemData), .data(RdData), .str(buffer_1_out), .clk(CLK), .ld(not_1_out),
    .clr(Reset));  // open: sel

  // Notes on the sheet:
  //   MemWrite: pull=down
endmodule

module Op_func_TO_Instr (
  input  op31,
  input  op30,
  input  op29,
  input  op28,
  input  op27,
  input  op26,
  input  fun5,
  input  fun4,
  input  fun3,
  input  fun2,
  input  fun1,
  input  fun0,
  output addu,
  output subu,
  output ori,
  output lui,
  output lw,
  output sw,
  output beq
);

  wire beq_out, buffer_1_out, buffer_2_out, buffer_3_out, buffer_4_out, buffer_5_out, buffer_6_out, lui_out,
       lw_out, not_1_out, not_2_out, not_3_out, not_4_out, not_5_out, not_6_out, not_7_out, ori_out,
       RType_out, sw_out;

  buf buffer_1 (buffer_1_out, op31);
  not not_1 (not_1_out, op31);
  not not_2 (not_2_out, op30);
  buf buffer_2 (buffer_2_out, op29);
  buf buffer_3 (buffer_3_out, op28);
  not not_3 (not_3_out, op29);
  buf buffer_4 (buffer_4_out, op27);
  not not_4 (not_4_out, op28);
  not not_5 (not_5_out, op27);
  buf buffer_5 (buffer_5_out, op26);
  not not_6 (not_6_out, op26);
  and RType (RType_out, not_1_out, not_2_out, not_3_out, not_4_out, not_5_out, not_6_out);
  and u_ori (ori_out, not_1_out, not_2_out, buffer_2_out, buffer_3_out, not_5_out, buffer_5_out);
  and u_lui (lui_out, not_1_out, not_2_out, buffer_2_out, buffer_3_out, buffer_4_out, buffer_5_out);
  and u_lw (lw_out, buffer_1_out, not_2_out, not_3_out, not_4_out, buffer_4_out, buffer_5_out);
  and u_sw (sw_out, buffer_1_out, not_2_out, buffer_2_out, not_4_out, buffer_4_out, buffer_5_out);
  and u_beq (beq_out, not_1_out, not_2_out, not_3_out, buffer_3_out, not_5_out, not_6_out);
  buf buffer_6 (buffer_6_out, fun1);
  not not_7 (not_7_out, fun1);
  buf buffer_7 (ori, ori_out);
  buf buffer_8 (lui, lui_out);
  buf buffer_9 (lw, lw_out);
  buf buffer_10 (sw, sw_out);
  buf buffer_11 (beq, beq_out);
  and u_addu (addu, RType_out, not_7_out);
  and u_subu (subu, RType_out, buffer_6_out);
endmodule

module EXT (
  input  [15:0] Din,
  input  ExtSign,
  output [31:0] Dout
);

  wire [31:0] bit_extender_1_out, bit_extender_2_out;

  assign bit_extender_1_out = {{16{1'b0}}, Din};  // Bit_Extender bit_extender_1
  assign bit_extender_2_out = {{16{Din[15]}}, Din};  // Bit_Extender bit_extender_2
  Multiplexer #(.width(32), .enable("false")) multiplexer_1 (
    .in0(bit_extender_1_out), .in1(bit_extender_2_out), .out(Dout), .sel(ExtSign));
endmodule

module NoBrchIFU (
  input  CLK,
  input  Reset,
  output [31:0] Instr
);

  wire [29:0] adder_1_out, PC_q;

  Clock clock_1 ();  // open: out
  Register #(.width(30)) PC (.D(adder_1_out), .Q(PC_q), .clk(CLK), .clr(Reset));  // open: en
  // Probe on PC_q
  // Probe on {PC_q[2:0], 2'b00}
  Adder #(.width(30)) adder_1 (.a(PC_q), .b(30'h1), .out(adder_1_out));  // open: cin, cout
  ROM #(.addrWidth(5), .dataWidth(32)) rom_1 (.addr({PC_q[2:0], 2'b00}), .data(Instr));  // open: sel
  // Probe on Instr

  // Notes on the sheet:
  //   contents of rom_1 (hex, n*v repeats v):
  //   34125125 125213 12344 2151211 9034097 214412 123213 12521521 21321312 15425215 55521 222133
endmodule

module Instr_TO_Ctl (
  input  addu,
  input  subu,
  input  ori,
  input  lw,
  input  sw,
  input  beq,
  output RegDst,
  output ALUSrc,
  output MemToReg,
  output RegWrite,
  output MemWrite,
  output nPC_sel,
  output ExtOp,
  output ALUctr_add,
  output ALUctr_sub,
  output ALUctr_or
);

  or u_RegDst (RegDst, addu, subu);
  buf buffer_1 (MemToReg, lw);
  or u_ALUSrc (ALUSrc, ori, lw, sw);
  or u_RegWrite (RegWrite, addu, subu, ori, lw);
  buf buffer_2 (MemWrite, sw);
  buf buffer_3 (nPC_sel, beq);
  or u_ExtOp (ExtOp, lw, sw);
  or ALUctr_2 (ALUctr_add, addu, lw, sw);
  or ALUctr_1 (ALUctr_sub, subu, beq);
  buf buffer_4 (ALUctr_or, ori);
endmodule

module Controller (
  input  [5:0] func,
  input  [5:0] op,
  output RegDst,
  output ALUSrc,
  output MemToReg,
  output RegWrite,
  output MemWrite,
  output nPC_sel,
  output ExtOp,
  output [2:0] ALUCtl
);

  wire op_func_to_instr_1_addu, op_func_to_instr_1_beq, op_func_to_instr_1_lw, op_func_to_instr_1_ori,
       op_func_to_instr_1_subu, op_func_to_instr_1_sw;

  Op_func_TO_Instr op_func_to_instr_1 (
    .addu(op_func_to_instr_1_addu), .subu(op_func_to_instr_1_subu), .ori(op_func_to_instr_1_ori),
    .lw(op_func_to_instr_1_lw), .sw(op_func_to_instr_1_sw), .beq(op_func_to_instr_1_beq), .op31(op[5]),
    .op30(op[4]), .op29(op[3]), .op28(op[2]), .op27(op[1]), .op26(op[0]), .fun5(func[5]), .fun4(func[4]),
    .fun3(func[3]), .fun2(func[2]), .fun1(func[1]), .fun0(func[0]));  // open: lui
  Instr_TO_Ctl instr_to_ctl_1 (
    .addu(op_func_to_instr_1_addu), .subu(op_func_to_instr_1_subu), .ori(op_func_to_instr_1_ori),
    .lw(op_func_to_instr_1_lw), .sw(op_func_to_instr_1_sw), .beq(op_func_to_instr_1_beq), .RegDst(RegDst),
    .ALUSrc(ALUSrc), .MemToReg(MemToReg), .RegWrite(RegWrite), .MemWrite(MemWrite), .nPC_sel(nPC_sel),
    .ExtOp(ExtOp), .ALUctr_add(ALUCtl[2]), .ALUctr_sub(ALUCtl[1]), .ALUctr_or(ALUCtl[0]));
endmodule

module InstrSplitter (
  input  [31:0] Instru,
  output [5:0] OpCode,
  output [5:0] func,
  output [4:0] _25_21,
  output [4:0] _20_16,
  output [4:0] _15_11,
  output [15:0] Imm
);


  assign _15_11 = Instru[15:11];
  assign _20_16 = Instru[20:16];
  assign _25_21 = Instru[25:21];
  assign func = Instru[5:0];
  assign Imm = Instru[15:0];
  assign OpCode = Instru[31:26];
endmodule

module Lshifter (
  input  [31:0] Din,
  input  [4:0] ShiftCnt,
  output [31:0] Dout
);

  Shifter #(.width(32)) shifter_1 (.in(Din), .\dist (ShiftCnt), .out(Dout));
endmodule
